# Fritzing sketch instrument prototype 1 (saved by Fritzing 0.9.3b)
breadboards: 1

parts:
  J1 = Piezo Speaker
  hc-sr1 = hc-sr04
  Part1 = Arduino Uno (Rev3)
  R1 = Resistor [tolerance=±5% resistance=1M package=THT]

nets:
  GND: J1.pin1, hc-sr1.GND, Part1.GND
  N1: J1.pin2, Part1.D10_PWM/SS
  VCC: hc-sr1.VCC, Part1.5V
  N2: hc-sr1.Trig, Part1.D2
  N3: hc-sr1.Echo, Part1.D3_PWM
  N4: Part1.D9_PWM, R1.Pin_0
  N5: Part1.D4, R1.Pin_1
